// Logisim project Circuito completo.circ as structural Verilog: 1 circuit, main circuit main
module main (
  input  reset,
  input  clock,
  input  eject,
  input  play,
  input  pause,
  input  stop,
  input  disco,
  output bandeja,
  output reproductor,
  output motor
);

  wire a, and_1_out, and_2_out, and_3_out, b, c, contador, not_1_out, not_2_out, not_3_out, not_4_out,
       not_5_out, not_6_out, not_7_out;

  not not_1 (not_1_out, c);
  and and_1 (and_1_out, a, b, not_1_out);
  flip_flops_main main_1 (
    .eject(eject), .play(play), .pause(pause), .stop(stop), .disco(disco), .contador(contador), .a(a), .b(b),
    .c(c), .reset(reset), .clock(clock));
  Counter #(.width(7), .max('h60)) counter_1 (
    .carry(contador), .clk(and_2_out), .clr(and_3_out));  // open: load, D, count, Q
  and and_2 (and_2_out, clock, and_1_out);
  and and_3 (and_3_out, not_2_out, b, c);
  not not_2 (not_2_out, a);
  not not_3 (not_3_out, a);
  not not_4 (not_4_out, b);
  and and_4 (bandeja, not_3_out, not_4_out, c);
  not not_5 (not_5_out, b);
  and and_5 (reproductor, a, not_5_out, not_6_out);
  not not_6 (not_6_out, c);
  and and_6 (motor, a, not_7_out);
  not not_7 (not_7_out, b);

  // Notes on the sheet:
  //   Entradas:
  //   Contador (reloj de 3s):
  //   Salidas:
endmodule
