// Logisim project flip flops.circ as structural Verilog: 1 circuit, main circuit main
module main (
  input  reset,
  input  clock,
  input  eject,
  input  play,
  input  pause,
  input  stop,
  input  disco,
  input  contador,
  output a,
  output b,
  output c
);

  wire and_1_out, and_2_out, and_3_out, and_4_out, and_5_out, and_6_out, and_7_out, and_8_out, and_9_out,
       and_10_out, and_11_out, and_12_out, and_13_out, and_14_out, and_15_out, and_16_out, and_17_out,
       not_1_out, not_2_out, not_3_out, not_4_out, not_5_out, not_6_out, not_7_out, not_8_out, not_9_out,
       not_10_out, not_11_out, not_12_out, not_13_out, not_14_out, not_15_out, not_16_out, not_17_out,
       not_18_out, not_19_out, not_20_out, not_21_out, not_22_out, not_23_out, not_24_out, not_25_out,
       not_26_out, not_27_out, not_28_out, not_29_out, or_1_out, or_2_out, or_3_out;

  not not_1 (not_1_out, eject);
  not not_2 (not_2_out, pause);
  not not_3 (not_3_out, stop);
  not not_4 (not_4_out, b);
  and and_1 (and_1_out, not_1_out, not_2_out, not_3_out, contador);
  and and_2 (and_2_out, stop, a, not_4_out);
  and and_3 (and_3_out, play, b, c);
  or or_1 (or_1_out, and_1_out, and_2_out, and_3_out);
  T_Flip_Flop u_A (.clk(clock), .T(or_1_out), .Q(a), .reset(reset));  // open: Qn, preset, en
  not not_5 (not_5_out, b);
  not not_6 (not_6_out, eject);
  not not_7 (not_7_out, play);
  not not_8 (not_8_out, pause);
  not not_9 (not_9_out, stop);
  not not_10 (not_10_out, disco);
  not not_11 (not_11_out, eject);
  not not_12 (not_12_out, pause);
  not not_13 (not_13_out, stop);
  not not_14 (not_14_out, b);
  and and_4 (and_4_out, eject, a, not_5_out);
  and and_5 (and_5_out, not_6_out, not_7_out, not_8_out, not_9_out, not_10_out, b);
  and and_6 (and_6_out, eject, c);
  and and_7 (and_7_out, not_11_out, not_12_out, not_13_out, contador);
  and and_8 (and_8_out, stop, a, not_14_out);
  and and_9 (and_9_out, play, b, c);
  or or_2 (or_2_out, and_4_out, and_5_out, and_6_out, and_7_out, and_8_out, and_9_out);
  T_Flip_Flop u_B (.clk(clock), .T(or_2_out), .Q(b), .reset(reset));  // open: Qn, preset, en
  not not_15 (not_15_out, b);
  not not_16 (not_16_out, b);
  not not_17 (not_17_out, c);
  not not_18 (not_18_out, a);
  not not_19 (not_19_out, b);
  not not_20 (not_20_out, eject);
  not not_21 (not_21_out, pause);
  not not_22 (not_22_out, stop);
  not not_23 (not_23_out, b);
  not not_24 (not_24_out, c);
  not not_25 (not_25_out, eject);
  not not_26 (not_26_out, pause);
  not not_27 (not_27_out, stop);
  not not_28 (not_28_out, a);
  not not_29 (not_29_out, c);
  and and_10 (and_10_out, eject, not_15_out, c);
  and and_11 (and_11_out, pause, a, not_16_out, not_17_out);
  and and_12 (and_12_out, eject, not_18_out, not_19_out);
  and and_13 (and_13_out, not_20_out, not_21_out, not_22_out, contador);
  and and_14 (and_14_out, stop, a, not_23_out, not_24_out);
  and and_15 (and_15_out, play, b, c);
  and and_16 (and_16_out, play, a, c);
  and and_17 (and_17_out, disco, not_25_out, not_26_out, not_27_out, not_28_out, not_29_out);
  or or_3 (or_3_out, and_10_out, and_11_out, and_12_out, and_13_out, and_14_out, and_15_out, and_16_out, and_17_out);
  T_Flip_Flop u_C (.clk(clock), .T(or_3_out), .Q(c), .reset(reset));  // open: Qn, preset, en

  // Notes on the sheet:
  //   Flip Flops A,B y C:
endmodule
